# Fritzing sketch Teil_1_Breadboard (saved by Fritzing 0.9.3b)
breadboards: 1

parts:
  LED1 = LED - 5mm [color="Blue (430nm)" package="5 mm [THT]"]
  R1 = Resistor [tolerance=±5% resistance=1k package=THT]
  Part1 = Arduino Uno (Rev3)
  S1 = Pushbutton [package="[THT]"]
  S2 = Pushbutton [package="[THT]"]
  R3 = Resistor [tolerance=±5% resistance=1k package=THT]
  S3 = Pushbutton [package="[THT]"]
  R5 = Resistor [tolerance=±5% resistance=1k package=THT]
  LED2 = LED - 5mm [color="Yellow (595nm)" package="5 mm [THT]"]
  R4 = Resistor [tolerance=±5% resistance=1k package=THT]

nets:
  N1: LED1.cathode, Part1.GND, R3.Pin_0, LED2.cathode, R4.Pin_0
  N2: LED1.anode, R1.Pin_0
  N3: R1.Pin_1, Part1.D8
  N4: Part1.D6_PWM, S2.Pin_1, S2.Pin_2, R3.Pin_1
  N5: Part1.D7, S1.Pin_2, R4.Pin_1
  N6: Part1.5V, S1.Pin_3, S1.Pin_4, S2.Pin_3, S2.Pin_4, S3.Pin_1, S3.Pin_2
  N7: S3.Pin_3, S3.Pin_4, R5.Pin_1
  N8: R5.Pin_0, LED2.anode
