# Fritzing sketch Teil_3_Breadboard (saved by Fritzing 0.9.3b)
breadboards: 1

parts:
  LED1 = LED - 5mm [color="Blue (430nm)" package="5 mm [THT]"]
  R1 = Resistor [tolerance=±5% resistance=10k package=THT]
  Part1 = Arduino Uno (Rev3)
  R4 = Resistor [tolerance=±5% resistance=1k package=THT]
  R5 = Photocell (LDR) [package=THT]

nets:
  N1: LED1.cathode, Part1.GND, R4.Pin_0
  N2: LED1.anode, R1.Pin_0
  N3: R1.Pin_1, Part1.D9_PWM
  N4: Part1.A0, R4.Pin_1, R5.pin_1
  N5: Part1.5V, R5.pin_0
