# Fritzing sketch Teil_4_LED_Matrix (saved by Fritzing 0.9.3b)
breadboards: 1

parts:
  R1 = Resistor [tolerance=±5% resistance=10k package=THT]
  Part1 = Arduino Uno (Rev3)
  R2 = Resistor [tolerance=±5% resistance=10k package=THT]
  LED6 = LED - 5mm [color="Blue (430nm)" package="5 mm [THT]"]
  LED10 = LED - 5mm [color="Blue (430nm)" package="5 mm [THT]"]
  LED11 = LED - 5mm [color="Blue (430nm)" package="5 mm [THT]"]
  LED12 = LED - 5mm [color="Blue (430nm)" package="5 mm [THT]"]
  LED13 = LED - 5mm [color="Blue (430nm)" package="5 mm [THT]"]
  LED14 = LED - 5mm [color="Blue (430nm)" package="5 mm [THT]"]
  LED15 = LED - 5mm [color="Blue (430nm)" package="5 mm [THT]"]
  LED16 = LED - 5mm [color="Blue (430nm)" package="5 mm [THT]"]

nets:
  N1: R1.Pin_0, LED6.cathode, LED10.cathode, LED11.cathode, LED15.cathode
  N2: R1.Pin_1, Part1.D7
  N3: Part1.D10_PWM/SS, LED15.anode, LED16.anode
  N4: Part1.D11_PWM/MOSI, LED11.anode, LED14.anode
  N5: Part1.D12/MISO, LED10.anode, LED13.anode
  N6: Part1.D13/SCK, LED6.anode, LED12.anode
  N7: Part1.D6_PWM, R2.Pin_1
  N8: R2.Pin_0, LED12.cathode, LED13.cathode, LED14.cathode, LED16.cathode
